// Logisim project 01_contador_flip-flop.circ as structural Verilog: 1 circuit, main circuit main
module main (
  input  in_1,
  output [3:0] out_2,
  output out_3,
  output out_4,
  output out_5,
  output out_6
);

  wire clock_1_out, t_ff_1_qn, t_ff_2_qn, t_ff_3_qn;

  Clock clock_1 (.out(clock_1_out));
  T_Flip_Flop t_ff_1 (.clk(clock_1_out), .T(in_1), .Q(out_2[0]), .Qn(t_ff_1_qn));  // open: preset, reset, en
  T_Flip_Flop t_ff_2 (.clk(t_ff_1_qn), .T(in_1), .Q(out_2[1]), .Qn(t_ff_2_qn));  // open: preset, reset, en
  T_Flip_Flop t_ff_3 (.clk(t_ff_2_qn), .T(in_1), .Q(out_2[2]), .Qn(t_ff_3_qn));  // open: preset, reset, en
  T_Flip_Flop t_ff_4 (.clk(t_ff_3_qn), .T(in_1), .Q(out_2[3]));  // open: Qn, preset, reset, en

  assign out_3 = out_2[0];
  assign out_4 = out_2[1];
  assign out_5 = out_2[2];
  assign out_6 = out_2[3];
endmodule
